# Fritzing sketch ProjetCasque (saved by Fritzing 0.9.4)
breadboards: 1

parts:
  Arduino_Nano = Arduino Nano (Rev3.0)
  R1 = Resistor [tolerance=±5% resistance=1.5k package=THT]
  VCC1 = Battery block 9V
  LED1 = LED - 5mm [color="Red (633nm)" package="5 mm [THT]"]
  LED2 = LED - 5mm [color="Red (633nm)" package="5 mm [THT]"]  # not connected
  LED3 = LED - 5mm [color="Red (633nm)" package="5 mm [THT]"]  # not connected
  LED4 = LED - 5mm [color="Red (633nm)" package="5 mm [THT]"]  # not connected
  LED5 = LED - 5mm [color="Red (633nm)" package="5 mm [THT]"]  # not connected
  LED6 = LED - 5mm [color="Red (633nm)" package="5 mm [THT]"]  # not connected
  J1 = Basic Servo
  J2 = Basic Servo
  J3 = Basic Servo
  BP = Pushbutton [package="[THT]"]
  R2 = Resistor [tolerance=±5% resistance=10k package=THT]

nets:
  N1: Arduino_Nano.GND, VCC1.+
  N2: Arduino_Nano.D2, J3.pulse
  N3: Arduino_Nano.D3, J2.pulse
  N4: Arduino_Nano.D4, J1.pulse
  N5: Arduino_Nano.D10, R1.Pin_0
  N6: Arduino_Nano.VIN, VCC1.-
  VCC: Arduino_Nano.5V, Arduino_Nano.D13/SCK, J1.vcc, J2.vcc, J3.vcc, R2.Pin_0
  N7: R1.Pin_1, LED1.anode
  GND: J1.gnd, J2.gnd, J3.gnd, BP.Pin_1, BP.Pin_2
  N8: BP.Pin_3, BP.Pin_4, R2.Pin_1
